// Digital circuit ntsc_gen.dig as structural Verilog
module ntsc_gen (
  input  _14_138MHZ
);

  wire _1V, _2H, _2V, _4H, _4V, _8H, _8V, _16H, _16V, _32H, _32V, _64H, _64V, _128H, _128V, _256H, _256V,
       _512H, _512V, _7408_1_pin3, _7408_1_pin6, _7408_1_pin8, _7408_1_pin11, _74060_1_p9, _74060_1_p14,
       _74060_1_p16, _74060_2_p14, _74060_2_p16, and_1_out, and_2_out, and_3_out, and_4_out, and_6_out,
       and_7_out, and_9_out, CLOCKHALF, HBLANK, HBLANK_t, HRESET, HRESET_t, HSYNC, nand_1_out,
       pulldown_15_out, VBLANK, VBLANK_t, VRESET, VRESET_t, VSYNC;

  LED led_1 (.in(_1V));
  LED led_2 (.in(_2V));
  LED led_3 (.in(_4V));
  LED led_4 (.in(_8V));
  LED led_5 (.in(_16V));
  LED led_6 (.in(_32V));
  LED led_7 (.in(_64V));
  LED led_8 (.in(_128V));
  LED led_9 (.in(_256V));
  LED led_10 (.in(_512V));
  LED led_11 (.in(_2H));
  LED led_12 (.in(_4H));
  LED led_13 (.in(_8H));
  LED led_14 (.in(_16H));
  LED led_15 (.in(_32H));
  LED led_16 (.in(_64H));
  LED led_17 (.in(_128H));
  LED led_18 (.in(_256H));
  LED led_19 (.in(_512H));
  PullDown pulldown_1 (.out(_2H));
  PullDown pulldown_2 (.out(_4H));
  PullDown pulldown_3 (.out(_8H));
  PullDown pulldown_4 (.out(_16H));
  PullDown pulldown_5 (.out(_32H));
  PullDown pulldown_6 (.out(_64H));
  PullDown pulldown_7 (.out(_128H));
  PullDown pulldown_8 (.out(_2V));
  PullDown pulldown_9 (.out(_4V));
  PullDown pulldown_10 (.out(_8V));
  PullDown pulldown_11 (.out(_16V));
  PullDown pulldown_12 (.out(_32V));
  PullDown pulldown_13 (.out(_64V));
  PullDown pulldown_14 (.out(_128V));
  PullDown pulldown_15 (.out(pulldown_15_out));
  // _74060 _74060_1: pin names not known; wires that end beside it: _2H, _4H, _8H, _16H, _32H, _64H, _128H, 1'b0, _74060_1_p9, _512H, _256H, 1'b1, CLOCKHALF, _74060_1_p14, _14_138MHZ, _74060_1_p16, _14_138MHZ, HRESET_t
  PullDown pulldown_16 (.out(_74060_1_p9));
  // _74060 _74060_2: pin names not known; wires that end beside it: _2V, _4V, _8V, _16V, _32V, _64V, _128V, 1'b0, pulldown_15_out, _512V, _256V, 1'b1, _1V, _74060_2_p14, HRESET, _74060_2_p16, HRESET, VRESET
  PullDown pulldown_17 (.out(_512H));
  PullDown pulldown_18 (.out(CLOCKHALF));
  PullDown pulldown_19 (.out(_74060_1_p14));
  PullDown pulldown_20 (.out(_74060_1_p16));
  PullDown pulldown_21 (.out(_512V));
  PullDown pulldown_22 (.out(_1V));
  PullDown pulldown_23 (.out(_74060_2_p14));
  PullDown pulldown_24 (.out(_74060_2_p16));
  PullDown pulldown_25 (.out(_256V));
  PullDown pulldown_26 (.out(_256H));
  // Probe 1V on _1V
  // Probe 2V on _2V
  // Probe 4V on _4V
  // Probe 8V on _8V
  // Probe 16V on _16V
  // Probe 32V on _32V
  // Probe 64V on _64V
  // Probe 128V on _128V
  // Probe 256V on _256V
  // Probe 512V on _512V
  // Probe 2H on _2H
  // Probe 4H on _4H
  // Probe 8H on _8H
  // Probe 16H on _16H
  // Probe 32H on _32H
  // Probe 64H on _64H
  // Probe 128H on _128H
  // Probe 256H on _256H
  // Probe 512H on _512H
  nor nor_1 (VBLANK_t, VRESET_t, VBLANK);
  nor nor_2 (VBLANK, VBLANK_t, _16V);
  and and_1 (and_1_out, VBLANK, _8V);
  nand nand_1 (nand_1_out, _16H, _64H);
  _7408 _7408_1 (
    .pin1(_2H), .pin2(_4H), .pin3(_7408_1_pin3), .pin4(_64H), .pin5(_128H), .pin6(_7408_1_pin6), .pin7(1'b0),
    .pin8(_7408_1_pin8), .pin9(_256H), .pin10(_7408_1_pin6), .pin11(_7408_1_pin11), .pin12(_7408_1_pin8),
    .pin13(_7408_1_pin3), .pin14(1'b1));
  and and_2 (and_2_out, _2H, _4H);
  and and_3 (and_3_out, _64H, _128H);
  and and_4 (and_4_out, _1V, _4V);
  and and_5 (VSYNC, and_1_out, _4V);
  nand nand_2 (HBLANK_t, nand_1_out, HBLANK);
  nand nand_3 (HBLANK, HBLANK_t, HRESET_t);
  and and_6 (and_6_out, and_3_out, _256H);
  LED led_20 (.in(_7408_1_pin11));
  and and_7 (and_7_out, and_2_out, and_6_out);
  and and_8 (HSYNC, HBLANK, _32H);
  and and_9 (and_9_out, and_4_out, _256V);
  D_FF d_ff_1 (.D(and_7_out), .C(_14_138MHZ), .Q(HRESET), .nQ(HRESET_t));
  // ScopeTrigger #(.maxStepCount(60), .trigger("rising")) scopetrigger_1: pin names not known; wires that end beside it: and_9_out
  D_FF d_ff_2 (.D(and_9_out), .C(HRESET), .Q(VRESET_t), .nQ(VRESET));

  // Other names for the same wires on the sheet: MAINCLOCK = _14_138MHZ

  // Notes on the sheet:
  //   _14_138MHZ: Hz: 20000
  //   Vertical Timer
  //   Horizontal Timer
  //   PIXELACTIVATE
  //   HRESET
  //   VRESET&VSYNC
  //   HBLANK
endmodule
